# Fritzing sketch L-Canbus-BTSheild-v5 (saved by Fritzing 0.9.2b)
circuit board: 4.7cm x 3.3cm
breadboards: 1

parts:
  J2 = female pin header, 9 pins [form="♀ (female)"]
  J1 = female pin header, 9 pins [form="♀ (female)"]
  Pad1 = Pad [width=1 height=2 connect=center]
  Pad2 = Pad [width=1 height=2 connect=center]
  Pad3 = Pad [width=1 height=2 connect=center]  # not connected
  Pad4 = Pad [width=1 height=2 connect=center]  # not connected
  Pad5 = Pad [width=1 height=2 connect=center]  # not connected
  Pad6 = Pad [width=1 height=2 connect=center]  # not connected
  Pad7 = Pad [width=1 height=2 connect=center]  # not connected
  Pad8 = Pad [width=1 height=2 connect=center]  # not connected
  Pad9 = Pad [width=1 height=2 connect=center]  # not connected
  Pad10 = Pad [width=1 height=2 connect=center]  # not connected
  Pad11 = Pad [width=1 height=2 connect=center]  # not connected
  Pad12 = Pad [width=1 height=2 connect=center]
  Pad13 = Pad [width=1 height=2 connect=center]
  Pad14 = Pad [width=1 height=2 connect=center]  # not connected
  Pad15 = Pad [width=1 height=2 connect=center]
  Pad16 = Pad [width=1 height=2 connect=center]  # not connected
  Pad17 = Pad [width=1 height=2 connect=center]  # not connected
  Pad18 = Pad [width=1 height=2 connect=center]  # not connected
  Pad19 = Pad [width=1 height=2 connect=center]  # not connected
  Pad20 = Pad [width=1 height=2 connect=center]  # not connected
  Pad21 = Pad [width=1 height=2 connect=center]  # not connected
  Pad22 = Pad [width=1 height=2 connect=center]  # not connected
  Pad23 = Pad [width=1 height=2 connect=center]  # not connected
  Pad24 = Pad [width=1 height=2 connect=center]  # not connected
  Pad25 = Pad [width=1 height=2 connect=center]  # not connected
  Pad26 = Pad [width=1 height=2 connect=center]  # not connected
  Pad27 = Pad [width=1 height=2 connect=center]  # not connected
  Pad28 = Pad [width=1 height=2 connect=center]  # not connected
  Pad29 = Pad [width=1 height=2 connect=center]  # not connected
  Pad30 = Pad [width=1 height=2 connect=center]  # not connected
  Pad31 = Pad [width=1 height=2 connect=center]  # not connected
  Pad32 = Pad [width=1 height=2 connect=center]  # not connected
  Pad33 = Pad [width=1 height=2 connect=center]  # not connected
  Pad34 = Pad [width=1 height=2 connect=center]  # not connected
  R5 = Resistor [tolerance=±5% resistance=1k package="0805 [SMD]"]
  R6 = Resistor [tolerance=±5% resistance=2.2k package="0805 [SMD]"]
  R3 = Resistor [tolerance=±5% resistance=470 package="0805 [SMD]"]
  R4 = Resistor [tolerance=±5% resistance=470 package="0805 [SMD]"]
  LED3 = smd LED [color="Blue (525nm)" package="1206 [SMD]"]
  LED1 = smd LED [color="Green (570nm)" package="1206 [SMD]"]
  IC1 = Voltage Regulator LM1117 [package=sot223]

nets:
  N1: J2.pin1, R4.Pin_1
  N2: J2.pin9, IC1.ADJ
  N3: J1.pin1, Pad13.pad
  N4: J1.pin2, R5.Pin_1
  N5: J1.pin9, Pad1.pad, R6.Pin_1, LED3.cathode, LED1.cathode, IC1.OUT
  N6: Pad2.pad, IC1.IN
  N7: Pad12.pad, R5.Pin_0, R6.Pin_0
  N8: Pad15.pad, R3.Pin_1
  N9: R3.Pin_0, LED3.anode
  N10: R4.Pin_0, LED1.anode

notes:
  CANBusGateway
  http://development.thecongers.org/
  CAN
  BT
